// Logisim project alu.circ as structural Verilog: 1 circuit, main circuit myALU
module myALU (
  input  [31:0] Input1,
  input  [31:0] Input2,
  output zero,
  output [31:0] Result
);

  Comparator #(.width(32)) comparator_1 (.a({32{1'b0}}), .b(Result), .eq(zero));  // open: gt, lt

  // Other names for the same wires on the sheet: in1[31:0] = Input1; in2[31:0] = Input2; res[31:0] = Result

  // Notes on the sheet:
  //   Inputs
  //   Outputs
endmodule
