// Logisim project control_unit.circ as structural Verilog: 1 circuit, main circuit control_unit
module control_unit (
  input  [5:0] six_upper_bits_of_instr,
  output Reg_Dest,
  output Jump,
  output Branch,
  output Mem_Read,
  output Mem_to_Reg,
  output Mem_Write,
  output ALU_Src,
  output Reg_Write
);

  PLA #(.in_width(6), .out_width(8), .\table ("000000 10000001 # If Opcode is 0, we are R-Type\n001000 00000010 # ADDi\n001001 00000010 # ADDiu\n001100 00000010 # ANDi\n001110 00000010 # XORi\n001101 00000010 # ORi\n000100 00010000 # BEQ\n000101 00010000 # BNE\n000110 00010000 # BLEZ\n000111 00010000 # BGTZ\n000001 00010000 # BGEZ\n100011 00011010 # LW\n101011 00000111 # SW\n100000 00011011 # LB\n101000 00000110 # SB\n001010 00000011 # SLTi\n001111 00000011 # Lui\n000010 01000000 # j\n000011 01000000 # JAL")) Program_Scheduler (
    .in(six_upper_bits_of_instr),
    .out({Reg_Dest, Jump, Branch, Mem_Read, Mem_to_Reg, Mem_Write, ALU_Src, Reg_Write}));

  // Other names for the same wires on the sheet: six_bit_in[5:0] = six_upper_bits_of_instr

  // Notes on the sheet:
  //   Input
  //   Outputs
  //   PLU_Logic
endmodule
